// Logisim project 1-Circuito.circ as structural Verilog: 1 circuit, main circuit main
module main (
  input  A,
  input  B,
  output out_3,
  output out_4,
  output out_5,
  output out_6,
  output out_7
);

  wire and_1_out, nand_1_out, nor_1_out, not_1_out, or_1_out;

  not not_1 (not_1_out, A);
  and and_1 (and_1_out, A, A, B);
  or or_1 (or_1_out, A, B);
  not not_2 (out_3, not_1_out);
  not not_3 (out_4, nand_1_out);
  nand nand_1 (nand_1_out, A, B, B);
  nor nor_1 (nor_1_out, A, B);
  not not_4 (out_5, nor_1_out);
  not not_5 (out_6, and_1_out);
  not not_6 (out_7, or_1_out);
endmodule
